# Fritzing sketch Schema (saved by Fritzing 0.9.3b)
breadboards: 2

parts:
  Součástka1 = Arduino Uno (Rev3) - ICSP
  Squix1 = OLED 0.96" 128x64 I2C SSD1306 (GND/VCC)
  DS1 = DS18B20 1-Wire Temperature Sensor Probe
  Součástka2 = Bluetooth HC-05 Macho
  DHT1 = DHT11 Humitidy and Temperature Sensor
  BMP280_Breakout1 = BMP280 Breakout Board [part_number=BMP280]

nets:
  N1: Součástka1.A4/SDA, Squix1.SCA, BMP280_Breakout1.SDA
  N2: Součástka1.A5/SCL, Squix1.SCL, BMP280_Breakout1.SCL
  N3: Součástka1.D10_PWM/SS, Součástka2.TXD
  N4: Součástka1.D11_PWM/MOSI, Součástka2.RXD
  GND: Součástka1.GND, Squix1.GND, DS1.GND, Součástka2.GND, DHT1.GND, BMP280_Breakout1.GND
  N5: Součástka1.D2, DS1.DQ
  N6: Součástka1.D5_PWM, DHT1.DATA
  VCC: Součástka1.3V3, Squix1.VCC, Součástka2.VCC, BMP280_Breakout1.VCC
  VDD: Součástka1.5V, DS1.VDD, DHT1.VDD

custom parts:
  OLED 0.96" 128x64 I2C SSD1306 (GND/VCC): OLED 0.96" 128x64 I2C SSD1306 Pinout: GND/VCC/SCL/SDA
  DHT11 Humitidy and Temperature Sensor: DHT11 Humidity and Temperature Sensor
  BMP280 Breakout Board: This is a breakout board for the Bosch Sensortec BMP280, "an absolute barometric pressure sensor especially designed for mobile applications." The operation range is 300 to 1100 hPa. Supply voltage is 1.2 to 3.6V. Operating temperature range is -40 to +85 °C.
